// Logisim project alu.circ as structural Verilog: 1 circuit, main circuit main
module main (
  input  in_1,
  input  [31:0] op1,
  input  in_3,
  input  [31:0] op2,
  input  [2:0] aluOP,
  output out_6,
  output out_7,
  output [31:0] \output ,
  output out_9,
  output zero_flag
);

  wire comparator_1_lt;
  wire [31:0] add, \and , \or , slt, sub;

  Adder #(.width(32)) adder_1 (.a(op1), .b(op2), .out(add), .cin(in_1), .cout(out_6));
  Subtractor #(.width(32)) subtractor_1 (.a(op1), .b(op2), .out(sub), .bin(in_3), .bout(out_7));
  assign \or  = op1 | op2;  // OR_Gate or, 32 bits wide
  assign \and  = op1 & op2;  // AND_Gate and, 32 bits wide
  Comparator #(.width(32)) comparator_1 (.a(op1), .b(op2), .gt(out_9), .eq(zero_flag), .lt(comparator_1_lt));
  assign slt = {{31{1'b0}}, comparator_1_lt};  // Bit_Extender bit_extender_1
  Multiplexer #(.select(3), .width(32), .enable("false")) multiplexer_1 (
    .in0(\and ), .in1(\or ), .in2(add), .in6(sub), .in7(slt), .out(\output ), .sel(aluOP));  // open: in3, in4, in5
endmodule
