// Logisim project resgister-file.circ as structural Verilog: 1 circuit, main circuit main
module main (
  input  [31:0] WriteData,
  input  [1:0] ReadRegister1,
  input  [1:0] ReadRegister2,
  input  RegWrite,
  input  [1:0] WriteRegister,
  output [31:0] ReadData1,
  output [31:0] ReadData2
);

  wire clock_1_out, decoder_1_out0, decoder_1_out1, decoder_1_out2, decoder_1_out3;
  wire [31:0] register_1_q, register_2_q, register_3_q, register_4_q;

  Decoder #(.select(2), .disabled(0)) decoder_1 (
    .out0(decoder_1_out0), .out1(decoder_1_out1), .out2(decoder_1_out2), .out3(decoder_1_out3),
    .sel(WriteRegister), .en(RegWrite));
  Clock clock_1 (.out(clock_1_out));
  Register #(.width(32)) register_1 (
    .D(WriteData), .en(decoder_1_out0), .Q(register_1_q), .clk(clock_1_out));  // open: clr
  Register #(.width(32)) register_2 (
    .D(WriteData), .en(decoder_1_out1), .Q(register_2_q), .clk(clock_1_out));  // open: clr
  Register #(.width(32)) register_3 (
    .D(WriteData), .en(decoder_1_out2), .Q(register_3_q), .clk(clock_1_out));  // open: clr
  Register #(.width(32)) register_4 (
    .D(WriteData), .en(decoder_1_out3), .Q(register_4_q), .clk(clock_1_out));  // open: clr
  Multiplexer #(.select(2), .width(32), .enable("false")) multiplexer_1 (
    .in0(register_1_q), .in1(register_2_q), .in2(register_3_q), .in3(register_4_q), .out(ReadData1),
    .sel(ReadRegister1));
  Multiplexer #(.select(2), .width(32), .enable("false")) multiplexer_2 (
    .in0(register_1_q), .in1(register_2_q), .in2(register_3_q), .in3(register_4_q), .out(ReadData2),
    .sel(ReadRegister2));
endmodule
